# Fritzing sketch sketch (saved by Fritzing 0.9.3b)
breadboards: 1

parts:
  R1 = Resistor [tolerance=±5% resistance=220 package=THT]
  R3 = Resistor [tolerance=±5% resistance=220 package=THT]
  Part1 = Arduino Uno (Rev3)
  Power_plug1 = Power plug
  U1 = V_REG_MIC2920 [package=sot223]
  U2 = ESP8266 WiFi Module [part_number=ESP8266]
  RFM12b1 = RFM12b HopeRF Transceiver

nets:
  N1: R1.Pin_0, Part1.D6_PWM
  N2: R1.Pin_1, R3.Pin_0, U2.TXD
  GND: R3.Pin_1, Part1.GND, Power_plug1.GND, U1.GND, U2.GND, RFM12b1.10_GND
  N3: Part1.D10_PWM/SS, RFM12b1.3_FSK/DATA
  N4: Part1.D7, U2.RXD
  N5: Part1.5V, RFM12b1.9_VDD
  N6: Power_plug1.VCC, U1.IN
  N7: U1.OUT, U2.VCC, U2.CH_PD
